// Logisim project ISA.circ as structural Verilog: 3 circuits, main circuit Main
module Main (
);

  wire Branch, Mem_read, Mem_write, MemToReg, RegWrite, ULAsrc;
  wire [1:0] RD, RS1, RS2;
  wire [3:0] IMM, OPCODE, ULA_CONTROL;
  wire [5:0] MINS_data;
  wire [11:0] b_reg_1_saida_1, b_reg_1_saida_2, bit_extender_1_out, multiplexer_1_out, PC_q;

  Register #(.width(12)) PC (.Q(PC_q));  // open: D, en, clk, clr
  Adder #(.width(12)) adder_1 (.a(PC_q), .b({12{1'b1}}));  // open: out, cin, cout
  ROM #(.addrWidth(12), .dataWidth(12)) MINS (.addr(PC_q), .data({OPCODE, RD, MINS_data}));
  ROM #(.addrWidth(4), .dataWidth(10)) UCONTROL (
    .addr(OPCODE), .data({RegWrite, ULA_CONTROL, ULAsrc, Mem_read, Mem_write, MemToReg, Branch}));
  assign bit_extender_1_out = {{8{IMM[3]}}, IMM};  // Bit_Extender bit_extender_1
  B_REG b_reg_1 (
    .RD(RD), .RS1(RS1), .RS2(RS2), .SAIDA_1(b_reg_1_saida_1), .SAIDA_2(b_reg_1_saida_2));  // open: DATA, CLK
  RAM #(.addrWidth(12), .dataWidth(12)) MDATA ();  // open: addr, we, oe, clk, din, dout
  Multiplexer #(.width(12)) multiplexer_1 (
    .in0(b_reg_1_saida_2), .in1(bit_extender_1_out), .out(multiplexer_1_out));  // open: sel
  ULA ula_1 (.rs1(b_reg_1_saida_1), .rs2(multiplexer_1_out), .ULA_CONTROL(ULA_CONTROL));  // open: ZERO, SAIDA

  // Notes on the sheet:
  //   contents of UCONTROL (hex, n*v repeats v):
  //   20a 302 3a2 142 16 307
endmodule

module ULA (
  input  [11:0] rs1,
  input  [11:0] rs2,
  input  [3:0] ULA_CONTROL,
  output ZERO,
  output [11:0] SAIDA
);

  wire comparator_1_lt;
  wire [11:0] adder_1_out, and_1_out, bit_extender_1_out, multiplexer_1_out, not_1_out, or_1_out,
       shifter_1_out, shifter_2_out, subtractor_1_out, xor_1_out;

  Adder #(.width(12)) adder_1 (.a(rs1), .b(rs2), .out(adder_1_out));  // open: cin, cout
  Subtractor #(.width(12)) subtractor_1 (.a(rs1), .b(rs2), .out(subtractor_1_out));  // open: bin, bout
  Shifter #(.width(12)) shifter_1 (.in(rs1), .\dist (4'b0001), .out(shifter_1_out));
  Shifter #(.shift("lr"), .width(12)) shifter_2 (.in(rs1), .\dist (4'b0001), .out(shifter_2_out));
  assign and_1_out = rs1 & rs2;  // AND_Gate and_1, 12 bits wide
  assign or_1_out = rs1 | rs2;  // OR_Gate or_1, 12 bits wide
  assign xor_1_out = rs1 ^ rs2;  // XOR_Gate xor_1, 12 bits wide
  assign not_1_out = ~rs1;  // NOT_Gate not_1, 12 bits wide
  Comparator #(.width(12)) comparator_1 (.a(rs1), .b(rs2), .lt(comparator_1_lt));  // open: gt, eq
  assign bit_extender_1_out = {{11{comparator_1_lt}}, comparator_1_lt};  // Bit_Extender bit_extender_1
  Multiplexer #(.select(4), .width(12)) multiplexer_1 (
    .in0(adder_1_out), .in1(subtractor_1_out), .in2(shifter_1_out), .in3(shifter_2_out), .in4(and_1_out),
    .in5(or_1_out), .in6(xor_1_out), .in7(not_1_out), .in8(bit_extender_1_out), .out(multiplexer_1_out),
    .sel(ULA_CONTROL));  // open: in9, in10, in11, in12, in13, in14, in15
  nor nor_1 (ZERO, multiplexer_1_out[0], multiplexer_1_out[1], multiplexer_1_out[2], multiplexer_1_out[3], multiplexer_1_out[4], multiplexer_1_out[5], multiplexer_1_out[6], multiplexer_1_out[7], multiplexer_1_out[8], multiplexer_1_out[9], multiplexer_1_out[10], multiplexer_1_out[11]);
endmodule

module B_REG (
  input  [11:0] DATA,
  input  CLK,
  input  [1:0] RD,
  input  [1:0] RS1,
  input  [1:0] RS2,
  output [11:0] SAIDA_1,
  output [11:0] SAIDA_2
);

  wire decoder_1_out0, decoder_1_out1, decoder_1_out2, decoder_1_out3;
  wire [11:0] R0, R1, R2, R3;

  Decoder #(.select(2)) decoder_1 (
    .out0(decoder_1_out0), .out1(decoder_1_out1), .out2(decoder_1_out2), .out3(decoder_1_out3), .sel(RD));  // open: en
  Register #(.width(12)) register_1 (.D(DATA), .en(decoder_1_out0), .Q(R0));  // open: clk, clr
  Register #(.width(12)) register_2 (.D(DATA), .en(decoder_1_out1), .Q(R1));  // open: clk, clr
  Register #(.width(12)) register_3 (.D(DATA), .en(decoder_1_out2), .Q(R2));  // open: clk, clr
  Register #(.width(12)) register_4 (.D(DATA), .en(decoder_1_out3), .Q(R3));  // open: clk, clr
  Multiplexer #(.select(2), .width(12)) multiplexer_1 (
    .in0(R0), .in1(R1), .in2(R2), .in3(R3), .out(SAIDA_1), .sel(RS1));
  Multiplexer #(.select(2), .width(12)) multiplexer_2 (
    .in0(R0), .in1(R1), .in2(R2), .in3(R3), .out(SAIDA_2), .sel(RS2));
endmodule
